# Fritzing sketch Irrigador (saved by Fritzing 1.0.0d)
breadboards: 1

parts:
  U2 = LuaNode32 / ESP32 [part_number=ESP32S-PIN30]
  Part1 = FC-28 Soil Hygrometer Module
  Part2 = FC-28 Soil Hygrometer Module - Probe
  M1 = 1 chan 5v relay module
  Power_plug1 = Power plug
  WATER_PUMP1 = water pump/motor

nets:
  N1: U2.D33, Part1.AO
  N2: U2.D2, M1.pin_3
  N3: Part1.VCC, M1.pin_1
  N4: Part1.GND, M1.pin_2
  N5: Part1.POS, Part2.POS
  N6: Part1.NEG, Part2.NEG
  N7: M1.pin_4, WATER_PUMP1.pin_1
  N8: M1.pin_5, Power_plug1.GND
  N9: Power_plug1.VCC, WATER_PUMP1.pin_2

custom parts:
  LuaNode32 / ESP32: New Image for LuaNode32 DOIT ESP32 DEVKIT V1. Base parts from LuaNode32 / ESP32 ESP32 based LuaNode32 by G.Noorlander DOIT Esp32 DevKit v1 (30 pins long, 11 pins width) by Werner Rothschopf (modified by vanepp Dec 2018)
  FC-28 Soil Hygrometer Module: The FC-28 is a soil hygrometer module that uses the Texas Instruments LM393 comparator chip to provide an analog measurement of soil humidity. The digital output is high when soil moisture is over a certain threshold, as determined by adjusting the potentiometer.
  FC-28 Soil Hygrometer Module - Probe: The FC-28 is a soil hygrometer module that uses the Texas Instruments LM393 comparator chip to provide an analog measurement of soil humidity.
  1 chan 5v relay module: 1 Channel 5V Relay Module Board Shield with Optocoupler Support High and Low Level Trigger for Arduino.
  water pump/motor: WATER PUMP BY ARDUBLOCKTR
